// Logisim project Logisim ATM System.circ as structural Verilog: 11 circuits, main circuit main
module main (
  input  in_1,
  input  clear
);

  wire _0_2_out, _0_out, _1_2_out, _1_out, _2_2_out, _2_out, _3_2_out, _3_out, _4_2_out,
       _4_bit_Encoder_active, _4_out, _5_2_out, _5_out, _6_2_out, _6_out, _7_2_out, _7_out, _8_2_out, _8_out,
       _9_2_out, _9_out, and_1_out, and_2_out, and_3_out, and_4_out, and_5_out, and_6_out, and_7_out,
       and_8_out, and_9_out, and_10_out, button_1_out, button_2_out, clock_1_out, clock_2_out, clock_3_out,
       clock_4_out, comparator_1_eq, comparator_2_eq, comparator_3_eq, comparator_4_eq, comparator_5_lt,
       comparator_6_gt, decoder_1_out0, decoder_1_out1, decoder_1_out2, decoder_1_out3, decoder_2_out1,
       decoder_2_out2, decoder_2_out3, Deposit_out, Enter_2_out, Enter_out, j_k_ff_1_q, j_k_ff_2_q,
       j_k_ff_3_q, j_k_ff_4_q, j_k_ff_5_q, MOD_10_Counter_2_q1, MOD_10_Counter_2_q2, MOD_10_Counter_2_q3,
       MOD_10_Counter_2_q4, MOD_10_Counter_q1, MOD_10_Counter_q2, MOD_10_Counter_q3, MOD_10_Counter_q4,
       n4_bit_encoder_1_active, n7_segment_decoder_1_a_2, n7_segment_decoder_1_b_2, n7_segment_decoder_1_c_2,
       n7_segment_decoder_1_d_2, n7_segment_decoder_1_e, n7_segment_decoder_1_f, n7_segment_decoder_1_g,
       n7_segment_decoder_2_a_2, n7_segment_decoder_2_b_2, n7_segment_decoder_2_c_2,
       n7_segment_decoder_2_d_2, n7_segment_decoder_2_e, n7_segment_decoder_2_f, n7_segment_decoder_2_g,
       nor_1_out, nor_2_out, not_1_out, not_2_out, not_3_out, not_4_out, or_1_out, or_2_out, Reset_2_out,
       Reset_out, Withdraw_out;
  wire [1:0] mod_3_counter_1_q2, MOD_3_Counter_2_q2;
  wire [3:0] _4_bit_Encoder_a1, n4_bit_encoder_1_a1, register_1_q, register_2_q, register_3_q, register_4_q,
       register_5_q, register_6_q, register_7_q, register_8_q, register_9_q, register_10_q, register_11_q;
  wire [7:0] adder_1_out, adder_2_out, adder_3_out, adder_4_out, bit_extender_1_out, bit_extender_2_out,
       bit_extender_3_out, multiplexer_1_out, multiplier_1_out, multiplier_2_out, register_12_q,
       register_13_q, subtractor_1_out;
  wire [15:0] rom_1_data, rom_2_data;

  _7_Segment_Display u_7_segment_display_1 (
    .g(n7_segment_decoder_1_g), .f(n7_segment_decoder_1_f), .a(n7_segment_decoder_1_a_2),
    .b(n7_segment_decoder_1_b_2), .e(n7_segment_decoder_1_e), .d(n7_segment_decoder_1_d_2),
    .c(n7_segment_decoder_1_c_2));  // open: dp
  _7_segment_decoder u_7_segment_decoder_1 (
    .D(MOD_10_Counter_q1), .C(MOD_10_Counter_q2), .B(MOD_10_Counter_q3), .A(MOD_10_Counter_q4),
    .a_2(n7_segment_decoder_1_a_2), .b_2(n7_segment_decoder_1_b_2), .c_2(n7_segment_decoder_1_c_2),
    .d_2(n7_segment_decoder_1_d_2), .e(n7_segment_decoder_1_e), .f(n7_segment_decoder_1_f),
    .g(n7_segment_decoder_1_g));
  TimeOutSensor MOD_10_Counter (
    .clock(clock_1_out), .Q4(MOD_10_Counter_q4), .Q3(MOD_10_Counter_q3), .Q2(MOD_10_Counter_q2),
    .Q1(MOD_10_Counter_q1));
  Button _2 (.out(_2_out));
  Button _1 (.out(_1_out));
  Button _5 (.out(_5_out));
  Button _4 (.out(_4_out));
  Button _8 (.out(_8_out));
  Button _7 (.out(_7_out));
  Button _0 (.out(_0_out));
  Button button_1 (.out(button_1_out));
  Clock clock_1 (.out(clock_1_out));
  nor nor_1 (nor_1_out, MOD_10_Counter_q4, MOD_10_Counter_q3, MOD_10_Counter_q2, MOD_10_Counter_q1);
  Button _3 (.out(_3_out));
  Button _6 (.out(_6_out));
  Button _9 (.out(_9_out));
  Button Enter (.out(Enter_out));
  or or_1 (or_1_out, Reset_out, nor_1_out);
  Button Reset (.out(Reset_out));
  Button button_2 (.out(button_2_out));
  MOD_3_Counter mod_3_counter_1 (
    .Clock(n4_bit_encoder_1_active), .Q2(mod_3_counter_1_q2[0]), .Q1(mod_3_counter_1_q2[1]), .Reset(or_1_out));
  Decoder #(.select(2)) decoder_1 (
    .out0(decoder_1_out0), .out1(decoder_1_out1), .out2(decoder_1_out2), .out3(decoder_1_out3),
    .sel(mod_3_counter_1_q2));  // open: en
  _4_bit_Encoder u_4_bit_encoder_1 (
    ._0(_0_out), ._1(_1_out), .A4(n4_bit_encoder_1_a1[3]), ._2(_2_out), ._3(_3_out), ._4(_4_out),
    .A3(n4_bit_encoder_1_a1[2]), ._5(_5_out), ._6(_6_out), ._7(_7_out), .A2(n4_bit_encoder_1_a1[1]),
    ._8(_8_out), ._9(_9_out), .A1(n4_bit_encoder_1_a1[0]), .Active(n4_bit_encoder_1_active));
  Register #(.width(4)) register_1 (
    .D(n4_bit_encoder_1_a1), .Q(register_1_q), .clk(decoder_1_out1), .clr(or_1_out));  // open: en
  Register #(.width(4)) register_2 (
    .D(n4_bit_encoder_1_a1), .Q(register_2_q), .clk(decoder_1_out2), .clr(or_1_out));  // open: en
  Register #(.width(4)) register_3 (
    .D(n4_bit_encoder_1_a1), .Q(register_3_q), .clk(decoder_1_out3), .clr(or_1_out));  // open: en
  Register #(.width(4)) register_4 (
    .D(n4_bit_encoder_1_a1), .Q(register_4_q), .clk(decoder_1_out0), .clr(or_1_out));  // open: en
  and and_1 (and_1_out, Enter_out, not_1_out, not_2_out);
  Register #(.width(4)) register_5 (
    .D(register_1_q), .Q(register_5_q), .clk(button_1_out), .clr(button_2_out));  // open: en
  Register #(.width(4)) register_6 (
    .D(register_2_q), .Q(register_6_q), .clk(button_1_out), .clr(button_2_out));  // open: en
  Register #(.width(4)) register_7 (
    .D(register_3_q), .Q(register_7_q), .clk(button_1_out), .clr(button_2_out));  // open: en
  Register #(.width(4)) register_8 (
    .D(register_4_q), .Q(register_8_q), .clk(button_1_out), .clr(button_2_out));  // open: en
  not not_1 (not_1_out, and_2_out);
  and and_2 (and_2_out, comparator_4_eq, comparator_2_eq, comparator_1_eq);
  J_K_Flip_Flop #(.trigger("falling")) j_k_ff_1 (
    .J(1'b1), .clk(and_1_out), .K(1'b1), .Q(j_k_ff_1_q));  // open: Qn, preset, en, reset
  Comparator #(.width(4)) comparator_1 (.a(register_1_q), .b(register_5_q), .eq(comparator_1_eq));  // open: gt, lt
  Comparator #(.width(4)) comparator_2 (.a(register_2_q), .b(register_6_q), .eq(comparator_2_eq));  // open: gt, lt
  Comparator #(.width(4)) comparator_3 (.a(register_3_q), .b(register_7_q), .eq(comparator_3_eq));  // open: gt, lt
  Comparator #(.width(4)) comparator_4 (.a(register_4_q), .b(register_8_q), .eq(comparator_4_eq));  // open: gt, lt
  J_K_Flip_Flop #(.trigger("falling")) j_k_ff_2 (
    .J(1'b1), .clk(j_k_ff_1_q), .K(1'b1), .Q(j_k_ff_2_q));  // open: Qn, preset, en, reset
  and and_3 (and_3_out, j_k_ff_1_q, j_k_ff_2_q);
  not not_2 (not_2_out, and_3_out);
  _7_Segment_Display u_7_segment_display_2 (
    .g(n7_segment_decoder_2_g), .f(n7_segment_decoder_2_f), .a(n7_segment_decoder_2_a_2),
    .b(n7_segment_decoder_2_b_2), .e(n7_segment_decoder_2_e), .d(n7_segment_decoder_2_d_2),
    .c(n7_segment_decoder_2_c_2));  // open: dp
  _7_segment_decoder u_7_segment_decoder_2 (
    .D(MOD_10_Counter_2_q1), .C(MOD_10_Counter_2_q2), .B(MOD_10_Counter_2_q3), .A(MOD_10_Counter_2_q4),
    .a_2(n7_segment_decoder_2_a_2), .b_2(n7_segment_decoder_2_b_2), .c_2(n7_segment_decoder_2_c_2),
    .d_2(n7_segment_decoder_2_d_2), .e(n7_segment_decoder_2_e), .f(n7_segment_decoder_2_f),
    .g(n7_segment_decoder_2_g));
  and and_4 (and_4_out, not_2_out, comparator_1_eq, comparator_2_eq, Enter_out, comparator_3_eq, comparator_4_eq);
  TimeOutSensor MOD_10_Counter_2 (
    .clock(and_5_out), .Q4(MOD_10_Counter_2_q4), .Q3(MOD_10_Counter_2_q3), .Q2(MOD_10_Counter_2_q2),
    .Q1(MOD_10_Counter_2_q1));
  nor nor_2 (nor_2_out, MOD_10_Counter_2_q4, MOD_10_Counter_2_q3, MOD_10_Counter_2_q2, MOD_10_Counter_2_q1);
  J_K_Flip_Flop j_k_ff_3 (.J(1'b1), .clk(and_4_out), .K(1'b1), .Q(j_k_ff_3_q));  // open: Qn, preset, en, reset
  and and_5 (and_5_out, j_k_ff_3_q, clock_2_out);
  Clock clock_2 (.out(clock_2_out));
  Button _1_2 (.out(_1_2_out));
  Button _4_2 (.out(_4_2_out));
  Button _7_2 (.out(_7_2_out));
  J_K_Flip_Flop j_k_ff_4 (.clk(nor_2_out), .Q(j_k_ff_4_q));  // open: J, K, Qn, preset, en, reset
  Button _2_2 (.out(_2_2_out));
  Button _5_2 (.out(_5_2_out));
  Button _8_2 (.out(_8_2_out));
  Button _0_2 (.out(_0_2_out));
  Button Reset_2 (.out(Reset_2_out));
  Button Deposit (.out(Deposit_out));
  Button Withdraw (.out(Withdraw_out));
  not not_3 (not_3_out, j_k_ff_4_q);
  Button _3_2 (.out(_3_2_out));
  Button _6_2 (.out(_6_2_out));
  Button _9_2 (.out(_9_2_out));
  Button Enter_2 (.out(Enter_2_out));
  and and_6 (and_6_out, Withdraw_out, j_k_ff_3_q);
  and and_7 (and_7_out, Deposit_out, j_k_ff_3_q);
  Decoder #(.select(2)) decoder_2 (
    .out1(decoder_2_out1), .out2(decoder_2_out2), .out3(decoder_2_out3), .sel(MOD_3_Counter_2_q2));  // open: out0, en
  Comparator comparator_5 (.a(adder_4_out), .b(register_12_q), .lt(comparator_5_lt));  // open: gt, eq
  J_K_Flip_Flop j_k_ff_5 (
    .J(1'b1), .clk(and_6_out), .K(1'b1), .Q(j_k_ff_5_q), .reset(and_7_out));  // open: Qn, preset, en
  Adder adder_1 (.a(adder_4_out), .b(register_12_q), .out(adder_1_out));  // open: cin, cout
  MOD_3_Counter MOD_3_Counter_2 (
    .Clock(_4_bit_Encoder_active), .Q2(MOD_3_Counter_2_q2[0]), .Q1(MOD_3_Counter_2_q2[1]), .Reset(Reset_2_out));
  not not_4 (not_4_out, j_k_ff_5_q);
  Comparator comparator_6 (.a(adder_1_out), .b({8{1'b1}}), .gt(comparator_6_gt));  // open: eq, lt
  Adder adder_2 (.a(adder_4_out), .b(register_12_q), .out(adder_2_out));  // open: cin, cout
  Subtractor subtractor_1 (.a(register_12_q), .b(adder_4_out), .out(subtractor_1_out));  // open: bin, bout
  and and_8 (and_8_out, comparator_5_lt, j_k_ff_5_q, Enter_2_out);
  and and_9 (and_9_out, Enter_2_out, not_4_out, comparator_6_gt);
  _4_bit_Encoder _4_bit_Encoder (
    ._0(_0_2_out), ._1(_1_2_out), .A4(_4_bit_Encoder_a1[3]), ._2(_2_2_out), ._3(_3_2_out), ._4(_4_2_out),
    .A3(_4_bit_Encoder_a1[2]), ._5(_5_2_out), ._6(_6_2_out), ._7(_7_2_out), .A2(_4_bit_Encoder_a1[1]),
    ._8(_8_2_out), ._9(_9_2_out), .A1(_4_bit_Encoder_a1[0]), .Active(_4_bit_Encoder_active));
  assign bit_extender_1_out = {{4{1'b0}}, register_9_q};  // Bit_Extender bit_extender_1
  Register #(.width(4)) register_9 (
    .D(_4_bit_Encoder_a1), .Q(register_9_q), .clk(decoder_2_out1), .clr(Reset_2_out));  // open: en
  Register #(.width(4)) register_10 (
    .D(_4_bit_Encoder_a1), .Q(register_10_q), .clk(decoder_2_out2), .clr(Reset_2_out));  // open: en
  assign bit_extender_2_out = {{4{1'b0}}, register_10_q};  // Bit_Extender bit_extender_2
  assign bit_extender_3_out = {{4{1'b0}}, register_11_q};  // Bit_Extender bit_extender_3
  Register #(.width(4)) register_11 (
    .D(_4_bit_Encoder_a1), .Q(register_11_q), .clk(decoder_2_out3), .clr(Reset_2_out));  // open: en
  Multiplexer #(.width(8)) multiplexer_1 (
    .in0(adder_2_out), .in1(subtractor_1_out), .out(multiplexer_1_out), .sel(j_k_ff_5_q));  // open: en
  and and_10 (and_10_out, or_2_out, not_3_out);
  or or_2 (or_2_out, and_8_out, and_9_out);
  Multiplier multiplier_1 (.a(8'h64), .b(bit_extender_1_out), .out(multiplier_1_out));  // open: cin, cout
  Multiplier multiplier_2 (.a(8'ha), .b(bit_extender_2_out), .out(multiplier_2_out));  // open: cin, cout
  Clock clock_3 (.out(clock_3_out));
  Register register_12 (.D(multiplexer_1_out), .en(and_10_out), .Q(register_12_q), .clk(clock_3_out), .clr(clear));
  Adder adder_3 (.a(multiplier_1_out), .b(multiplier_2_out), .out(adder_3_out));  // open: cin, cout
  Adder adder_4 (.a(adder_3_out), .b(bit_extender_3_out), .out(adder_4_out));  // open: cin, cout
  Register register_13 (.D(adder_4_out), .en(in_1), .Q(register_13_q), .clk(clock_4_out));  // open: clr
  Clock clock_4 (.out(clock_4_out));
  Hex_Digit_Display hex_digit_display_1 (.value(rom_1_data[15:12]));  // open: dp
  ROM #(.dataWidth(16)) rom_1 (.addr(register_12_q), .data(rom_1_data));  // open: sel
  Hex_Digit_Display hex_digit_display_2 (.value(rom_1_data[11:8]));  // open: dp
  ROM #(.dataWidth(16)) rom_2 (.addr(register_13_q), .data(rom_2_data));  // open: sel
  Hex_Digit_Display hex_digit_display_3 (.value(rom_1_data[7:4]));  // open: dp
  Hex_Digit_Display hex_digit_display_4 (.value(rom_2_data[15:12]));  // open: dp
  Hex_Digit_Display hex_digit_display_5 (.value(rom_1_data[3:0]));  // open: dp
  Hex_Digit_Display hex_digit_display_6 (.value(rom_2_data[11:8]));  // open: dp
  Hex_Digit_Display hex_digit_display_7 (.value(rom_2_data[7:4]));  // open: dp
  Hex_Digit_Display hex_digit_display_8 (.value(rom_2_data[3:0]));  // open: dp

  // Notes on the sheet:
  //   10second TimeOut
  //   4-bit_Decoder
  //   Setting PasWord
  //   StoredPIN_Reset
  //   Counter
  //   4-bit Encoder
  //   Input_PIN
  //   Stored_PIN
  //   10second TimeOut
  //   4-bit_Decoder
  //   1 is subbed, 0 is added
  //   contents of rom_1 (hex, n*v repeats v):
  //   0 1 2 3 4 5 6 7 8 9 10 11 12 13 14 15 16 17 18 19 20 21 22 23 24 25 26 27 28 29 30 31 32 33 34 35 36
  //   37 38 39 40 41 42 43 44 45 46 47 48 49 50 51 52 53 54 55 56 57 58 59 60 61 62 63 64 65 66 67 68 69
  //   70 71 72 73 74 75 76 77 78 79 80 81 82 83 84 85 86 87 88 89 90 91 92 93 94 95 96 97 98 99 100 101
  //   102 103 104 105 106 107 108 109 110 111 112 113 114 115 116 117 118 119 120 121 122 123 124 125 126
  //   127 128 129 130 131 132 133 134 135 136 137 138 139 140 141 142 143 144 145 146 147 148 149 150 151
  //   152 153 154 155 156 157 158 159 160 161 162 163 164 165 166 167 168 169 170 171 172 173 174 175 176
  //   177 178 179 180 181 182 183 184 185 186 187 188 189 190 191 192 193 194 195 196 197 198 199 200 201
  //   202 203 204 205 206 207 208 209 210 211 212 123 214 215 216 217 218 219 220 221 222 223 224 225 226
  //   227 228 229 230 231 232 233 234 235 236 237 238 239 240 241 242 243 244 245 246 247 248 249 250 251
  //   252 253 254 255
  //   contents of rom_2 (hex, n*v repeats v):
  //   0 1 2 3 4 5 6 7 8 9 10 11 12 13 14 15 16 17 18 19 20 21 22 23 24 25 26 27 28 29 30 31 32 33 34 35 36
  //   37 38 39 40 41 42 43 44 45 46 47 48 49 50 51 52 53 54 55 56 57 58 59 60 61 62 63 64 65 66 67 68 69
  //   70 71 72 73 74 75 76 77 78 79 80 81 82 83 84 85 86 87 88 89 90 91 92 93 94 95 96 97 98 99 100 101
  //   102 103 104 105 106 107 108 109 110 111 112 113 114 115 116 117 118 119 120 121 122 123 124 125 126
  //   127 128 129 130 131 132 133 134 135 136 137 138 139 140 141 142 143 144 145 146 147 148 149 150 151
  //   152 153 154 155 156 157 158 159 160 161 162 163 164 165 166 167 168 169 170 171 172 173 174 175 176
  //   177 178 179 180 181 182 183 184 185 186 187 188 189 190 191 192 193 194 195 196 197 198 199 200 201
  //   202 203 204 205 206 207 208 209 210 211 212 123 214 215 216 217 218 219 220 221 222 223 224 225 226
  //   227 228 229 230 231 232 233 234 235 236 237 238 239 240 241 242 243 244 245 246 247 248 249 250 251
  //   252 253 254 255
  //   b-a
  //   b-a
endmodule

module _4_bit_Encoder (
  input  _0,
  input  _1,
  input  _2,
  input  _3,
  input  _4,
  input  _5,
  input  _6,
  input  _7,
  input  _8,
  input  _9,
  output A4,
  output A3,
  output A2,
  output A1,
  output Active
);

  wire or_5_out, or_6_out;

  or or_1 (A4, _8, _9);
  or or_2 (A3, _4, _7, _6, _5);
  or or_3 (A2, _2, _3, _6, _7);
  or or_4 (A1, _1, _3, _5, _7, _9);
  or or_5 (or_5_out, _0, _1, _2, _3, _7);
  or or_6 (or_6_out, _4, _5, _6, _8, _9);
  or or_7 (Active, or_5_out, or_6_out);

  // Notes on the sheet:
  //   4-bit Encoder
endmodule

module Check_PassWord (
  input  [3:0] Input_PIN,
  output Output
);

  wire and_1_out, and_3_out, Enter_out, j_k_ff_1_q, j_k_ff_2_q, not_1_out, not_2_out, or_1_out;
  wire [3:0] xor_1_out;

  Button Enter (.out(Enter_out));
  assign xor_1_out = Input_PIN ^ 4'b0011;  // XOR_Gate xor_1, 4 bits wide
  or or_1 (or_1_out, xor_1_out[0], xor_1_out[1], xor_1_out[2], xor_1_out[3]);
  not not_1 (not_1_out, and_3_out);
  not not_2 (not_2_out, or_1_out);
  and and_1 (and_1_out, or_1_out, not_1_out, Enter_out);
  and and_2 (Output, not_1_out, Enter_out, not_2_out);
  J_K_Flip_Flop #(.trigger("falling")) j_k_ff_1 (
    .J(1'b1), .clk(and_1_out), .K(1'b1), .Q(j_k_ff_1_q));  // open: Qn, preset, en, reset
  and and_3 (and_3_out, j_k_ff_1_q, j_k_ff_2_q);
  J_K_Flip_Flop #(.trigger("falling")) j_k_ff_2 (
    .J(1'b1), .clk(j_k_ff_1_q), .K(1'b1), .Q(j_k_ff_2_q));  // open: Qn, preset, en, reset

  // Notes on the sheet:
  //   stored_PIN
endmodule

module MOD_3_Counter (
  input  Clock,
  input  Reset,
  output Q2,
  output Q1
);

  J_K_Flip_Flop j_k_ff_1 (.J(1'b1), .clk(Clock), .K(1'b1), .Q(Q2), .reset(Reset));  // open: Qn, preset, en
  J_K_Flip_Flop j_k_ff_2 (.J(Q2), .clk(Clock), .K(Q2), .Q(Q1), .reset(Reset));  // open: Qn, preset, en
  and and_1 (Reset, Q2, Q1);
endmodule

module TimeOutSensor (
  input  clock,
  output Q4,
  output Q3,
  output Q2,
  output Q1
);

  wire and_1_out, and_2_out, and_3_out;

  J_K_Flip_Flop j_k_ff_1 (.J(1'b1), .clk(clock), .K(1'b1), .Q(Q4), .reset(and_3_out));  // open: Qn, preset, en
  J_K_Flip_Flop j_k_ff_2 (.J(Q4), .clk(clock), .K(Q4), .Q(Q3), .reset(and_3_out));  // open: Qn, preset, en
  and and_1 (and_1_out, Q4, Q3);
  and and_2 (and_2_out, and_1_out, Q2);
  J_K_Flip_Flop j_k_ff_3 (
    .J(and_1_out), .clk(clock), .K(and_1_out), .Q(Q2), .reset(and_3_out));  // open: Qn, preset, en
  J_K_Flip_Flop j_k_ff_4 (
    .J(and_2_out), .clk(clock), .K(and_2_out), .Q(Q1), .reset(and_3_out));  // open: Qn, preset, en
  and and_3 (and_3_out, Q1, Q3);
endmodule

module _7_segment_decoder (
  input  D,
  input  C,
  input  B,
  input  A,
  output a_2,
  output b_2,
  output c_2,
  output d_2,
  output e,
  output f,
  output g
);

  wire and_1_out, and_2_out, and_3_out, and_4_out, and_5_out, and_6_out, and_7_out, and_8_out, and_9_out,
       and_10_out, and_11_out, and_12_out, and_13_out, and_14_out, and_15_out, and_16_out, not_1_out,
       not_2_out, not_3_out, not_4_out, not_5_out, not_6_out, not_7_out, not_8_out, not_9_out, not_10_out,
       not_11_out, not_12_out, not_13_out, not_14_out, not_15_out, not_16_out, not_17_out, not_18_out,
       not_19_out, not_20_out, not_21_out;

  not not_1 (not_1_out, C);
  and and_1 (and_1_out, not_1_out, not_2_out);
  not not_2 (not_2_out, A);
  and and_2 (and_2_out, C, A);
  not not_3 (not_3_out, C);
  not not_4 (not_4_out, B);
  and and_3 (and_3_out, not_4_out, not_5_out);
  not not_5 (not_5_out, A);
  and and_4 (and_4_out, B, A);
  not not_6 (not_6_out, B);
  or or_1 (c_2, not_6_out, A, C);
  not not_7 (not_7_out, C);
  and and_5 (and_5_out, not_7_out, not_8_out);
  not not_8 (not_8_out, A);
  not not_9 (not_9_out, C);
  and and_6 (and_6_out, not_9_out, B);
  and and_7 (and_7_out, B, not_10_out);
  not not_10 (not_10_out, A);
  and and_8 (and_8_out, C, not_11_out, A);
  not not_11 (not_11_out, B);
  not not_12 (not_12_out, C);
  and and_9 (and_9_out, not_12_out, not_13_out);
  not not_13 (not_13_out, A);
  and and_10 (and_10_out, B, not_14_out);
  not not_14 (not_14_out, A);
  not not_15 (not_15_out, B);
  and and_11 (and_11_out, not_15_out, not_16_out);
  not not_16 (not_16_out, A);
  and and_12 (and_12_out, C, not_17_out);
  not not_17 (not_17_out, B);
  and and_13 (and_13_out, C, not_18_out);
  not not_18 (not_18_out, A);
  not not_19 (not_19_out, C);
  and and_14 (and_14_out, not_19_out, B);
  and and_15 (and_15_out, C, not_20_out);
  not not_20 (not_20_out, B);
  and and_16 (and_16_out, C, not_21_out);
  not not_21 (not_21_out, A);
  or or_2 (a_2, and_1_out, B, and_2_out, D);
  or or_3 (b_2, not_3_out, and_3_out, and_4_out);
  or or_4 (d_2, and_5_out, and_6_out, and_7_out, and_8_out, D);
  or or_5 (e, and_9_out, and_10_out);
  or or_6 (f, and_11_out, and_12_out, and_13_out, D);
  or or_7 (g, and_14_out, and_15_out, and_16_out, D);
endmodule

module try (
  input  in_1
);

  wire _0_out, _1_out, _2_out, _3_out, _4_out, _5_out, _6_out, _7_out, _8_out, _9_out, clock_1_out,
       decoder_1_out1, decoder_1_out2, decoder_1_out3, Enter_out, n4_bit_encoder_1_active, Reset_out;
  wire [1:0] mod_3_counter_1_q2;
  wire [3:0] n4_bit_encoder_1_a1, register_1_q, register_2_q, register_3_q;
  wire [7:0] adder_1_out, adder_2_out, bit_extender_1_out, bit_extender_2_out, bit_extender_3_out,
       multiplier_1_out, multiplier_2_out, register_4_q;
  wire [15:0] rom_1_data;

  Button _2 (.out(_2_out));
  Button _1 (.out(_1_out));
  Button _4 (.out(_4_out));
  Button _5 (.out(_5_out));
  Button _8 (.out(_8_out));
  Button _7 (.out(_7_out));
  Button _0 (.out(_0_out));
  Button Reset (.out(Reset_out));
  Button _3 (.out(_3_out));
  Button _6 (.out(_6_out));
  Button _9 (.out(_9_out));
  Button Enter (.out(Enter_out));
  MOD_3_Counter mod_3_counter_1 (
    .Clock(n4_bit_encoder_1_active), .Q2(mod_3_counter_1_q2[0]), .Q1(mod_3_counter_1_q2[1]), .Reset(Reset_out));
  Decoder #(.select(2)) decoder_1 (
    .out1(decoder_1_out1), .out2(decoder_1_out2), .out3(decoder_1_out3), .sel(mod_3_counter_1_q2));  // open: out0, en
  _4_bit_Encoder u_4_bit_encoder_1 (
    ._0(_0_out), ._1(_1_out), .A4(n4_bit_encoder_1_a1[3]), ._2(_2_out), ._3(_3_out), ._4(_4_out),
    .A3(n4_bit_encoder_1_a1[2]), ._5(_5_out), ._6(_6_out), ._7(_7_out), .A2(n4_bit_encoder_1_a1[1]),
    ._8(_8_out), ._9(_9_out), .A1(n4_bit_encoder_1_a1[0]), .Active(n4_bit_encoder_1_active));
  Register #(.width(4)) register_1 (
    .D(n4_bit_encoder_1_a1), .Q(register_1_q), .clk(decoder_1_out1), .clr(Reset_out));  // open: en
  Register #(.width(4)) register_2 (
    .D(n4_bit_encoder_1_a1), .Q(register_2_q), .clk(decoder_1_out2), .clr(Reset_out));  // open: en
  Register #(.width(4)) register_3 (
    .D(n4_bit_encoder_1_a1), .Q(register_3_q), .clk(decoder_1_out3), .clr(Reset_out));  // open: en
  assign bit_extender_1_out = {{4{1'b0}}, register_1_q};  // Bit_Extender bit_extender_1
  assign bit_extender_2_out = {{4{1'b0}}, register_2_q};  // Bit_Extender bit_extender_2
  assign bit_extender_3_out = {{4{1'b0}}, register_3_q};  // Bit_Extender bit_extender_3
  Multiplier multiplier_1 (.a(8'h64), .b(bit_extender_1_out), .out(multiplier_1_out));  // open: cin, cout
  Multiplier multiplier_2 (.a(8'ha), .b(bit_extender_2_out), .out(multiplier_2_out));  // open: cin, cout
  Adder adder_1 (.a(multiplier_1_out), .b(multiplier_2_out), .out(adder_1_out));  // open: cin, cout
  Adder adder_2 (.a(adder_1_out), .b(bit_extender_3_out), .out(adder_2_out));  // open: cin, cout
  Clock clock_1 (.out(clock_1_out));
  Register register_4 (.D(adder_2_out), .en(in_1), .Q(register_4_q), .clk(clock_1_out));  // open: clr
  Hex_Digit_Display hex_digit_display_1 (.value(rom_1_data[15:12]));  // open: dp
  ROM #(.dataWidth(16)) rom_1 (.addr(register_4_q), .data(rom_1_data));  // open: sel
  Hex_Digit_Display hex_digit_display_2 (.value(rom_1_data[11:8]));  // open: dp
  Hex_Digit_Display hex_digit_display_3 (.value(rom_1_data[7:4]));  // open: dp
  Hex_Digit_Display hex_digit_display_4 (.value(rom_1_data[3:0]));  // open: dp

  // Notes on the sheet:
  //   contents of rom_1 (hex, n*v repeats v):
  //   0 1 2 3 4 5 6 7 8 9 10 11 12 13 14 15 16 17 18 19 20 21 22 23 24 25 26 27 28 29 30 31 32 33 34 35 36
  //   37 38 39 40 41 42 43 44 45 46 47 48 49 50 51 52 53 54 55 56 57 58 59 60 61 62 63 64 65 66 67 68 69
  //   70 71 72 73 74 75 76 77 78 79 80 81 82 83 84 85 86 87 88 89 90 91 92 93 94 95 96 97 98 99 100 101
  //   102 103 104 105 106 107 108 109 110 111 112 113 114 115 116 117 118 119 120 121 122 123 124 125 126
  //   127 128 129 130 131 132 133 134 135 136 137 138 139 140 141 142 143 144 145 146 147 148 149 150 151
  //   152 153 154 155 156 157 158 159 160 161 162 163 164 165 166 167 168 169 170 171 172 173 174 175 176
  //   177 178 179 180 181 182 183 184 185 186 187 188 189 190 191 192 193 194 195 196 197 198 199 200 201
  //   202 203 204 205 206 207 208 209 210 211 212 123 214 215 216 217 218 219 220 221 222 223 224 225 226
  //   227 228 229 230 231 232 233 234 235 236 237 238 239 240 241 242 243 244 245 246 247 248 249 250 251
  //   252 253 254 255
  //   b-a
endmodule

module MOD_2Counter (
  input  Clock,
  input  Pause,
  output Q2,
  output Q1
);

  wire and_1_out, and_2_out;

  and and_1 (and_1_out, Clock, Pause);
  J_K_Flip_Flop j_k_ff_1 (.J(1'b1), .clk(and_1_out), .K(1'b1), .Q(Q2), .reset(and_2_out));  // open: Qn, preset, en
  J_K_Flip_Flop j_k_ff_2 (.J(Q2), .clk(and_1_out), .K(Q2), .Q(Q1), .reset(and_2_out));  // open: Qn, preset, en
  and and_2 (and_2_out, Q2, Q1);
endmodule

module MOD_10_Counter (
  input  clock,
  input  reset_hour_2,
  input  pause,
  output Q4,
  output Q3,
  output Q2,
  output Q1
);

  wire and_1_out, and_2_out, and_3_out, and_4_out, or_1_out;

  J_K_Flip_Flop j_k_ff_1 (.J(1'b1), .clk(and_1_out), .K(1'b1), .Q(Q4), .reset(or_1_out));  // open: Qn, preset, en
  and and_1 (and_1_out, clock, pause);
  J_K_Flip_Flop j_k_ff_2 (.J(Q4), .clk(and_1_out), .K(Q4), .Q(Q3), .reset(or_1_out));  // open: Qn, preset, en
  and and_2 (and_2_out, Q4, Q3);
  and and_3 (and_3_out, and_2_out, Q2);
  J_K_Flip_Flop j_k_ff_3 (
    .J(and_2_out), .clk(and_1_out), .K(and_2_out), .Q(Q2), .reset(or_1_out));  // open: Qn, preset, en
  J_K_Flip_Flop j_k_ff_4 (
    .J(and_3_out), .clk(and_1_out), .K(and_3_out), .Q(Q1), .reset(or_1_out));  // open: Qn, preset, en
  or or_1 (or_1_out, and_4_out, reset_hour_2);
  and and_4 (and_4_out, Q3, Q1);
endmodule

module MOD_6_Counter (
  input  clock,
  input  pause,
  output Q4,
  output Q3,
  output Q2,
  output Q1
);

  wire and_1_out, and_2_out, and_3_out, and_4_out;

  and and_1 (and_1_out, clock, pause);
  J_K_Flip_Flop j_k_ff_1 (.J(1'b1), .clk(and_1_out), .K(1'b1), .Q(Q4), .reset(and_4_out));  // open: Qn, preset, en
  and and_2 (and_2_out, Q4, Q3);
  J_K_Flip_Flop j_k_ff_2 (.J(Q4), .clk(and_1_out), .K(Q4), .Q(Q3), .reset(and_4_out));  // open: Qn, preset, en
  J_K_Flip_Flop j_k_ff_3 (
    .J(and_2_out), .clk(and_1_out), .K(and_2_out), .Q(Q2), .reset(and_4_out));  // open: Qn, preset, en
  and and_3 (and_3_out, and_2_out, Q2);
  J_K_Flip_Flop j_k_ff_4 (
    .J(and_3_out), .clk(and_1_out), .K(and_3_out), .Q(Q1), .reset(and_4_out));  // open: Qn, preset, en
  and and_4 (and_4_out, Q2, Q3);
endmodule

module MOD_10_Counter_2 (
  input  clock,
  input  pause,
  output Q4,
  output Q3,
  output Q2,
  output Q1
);

  wire and_1_out, and_2_out, and_3_out, and_4_out;

  and and_1 (and_1_out, clock, pause);
  J_K_Flip_Flop j_k_ff_1 (.J(1'b1), .clk(and_1_out), .K(1'b1), .Q(Q4), .reset(and_4_out));  // open: Qn, preset, en
  and and_2 (and_2_out, Q4, Q3);
  J_K_Flip_Flop j_k_ff_2 (.J(Q4), .clk(and_1_out), .K(Q4), .Q(Q3), .reset(and_4_out));  // open: Qn, preset, en
  J_K_Flip_Flop j_k_ff_3 (
    .J(and_2_out), .clk(and_1_out), .K(and_2_out), .Q(Q2), .reset(and_4_out));  // open: Qn, preset, en
  and and_3 (and_3_out, and_2_out, Q2);
  J_K_Flip_Flop j_k_ff_4 (
    .J(and_3_out), .clk(and_1_out), .K(and_3_out), .Q(Q1), .reset(and_4_out));  // open: Qn, preset, en
  and and_4 (and_4_out, Q1, Q3);
endmodule
