// Logisim project Logisim Digital PassWord System.circ as structural Verilog: 6 circuits, main circuit main
module main (
  output OutPut
);

  wire _0_out, _1_out, _2_out, _3_out, _4_out, _5_out, _6_out, _7_out, _8_out, _9_out, and_1_out,
       button_1_out, button_2_out, clock_1_out, comparator_1_eq, comparator_2_eq, comparator_3_eq,
       comparator_4_eq, decoder_1_out0, decoder_1_out1, decoder_1_out2, decoder_1_out3, Enter_out,
       j_k_ff_1_q, n4_bit_encoder_1_active, n7_segment_decoder_1_a_2, n7_segment_decoder_1_b_2,
       n7_segment_decoder_1_c_2, n7_segment_decoder_1_d_2, n7_segment_decoder_1_e, n7_segment_decoder_1_f,
       n7_segment_decoder_1_g, nor_1_out, or_1_out, Reset_out, TimeOut_q1, TimeOut_q2, TimeOut_q3, TimeOut_q4;
  wire [1:0] mod_3_counter_1_q2;
  wire [3:0] n4_bit_encoder_1_a1, register_1_q, register_2_q, register_3_q, register_4_q, register_5_q,
       register_6_q, register_7_q, register_8_q;

  _7_Segment_Display u_7_segment_display_1 (
    .g(n7_segment_decoder_1_g), .f(n7_segment_decoder_1_f), .a(n7_segment_decoder_1_a_2),
    .b(n7_segment_decoder_1_b_2), .e(n7_segment_decoder_1_e), .d(n7_segment_decoder_1_d_2),
    .c(n7_segment_decoder_1_c_2));  // open: dp
  _7_segment_decoder u_7_segment_decoder_1 (
    .D(TimeOut_q1), .C(TimeOut_q2), .B(TimeOut_q3), .A(TimeOut_q4), .a_2(n7_segment_decoder_1_a_2),
    .b_2(n7_segment_decoder_1_b_2), .c_2(n7_segment_decoder_1_c_2), .d_2(n7_segment_decoder_1_d_2),
    .e(n7_segment_decoder_1_e), .f(n7_segment_decoder_1_f), .g(n7_segment_decoder_1_g));
  TimeOutSensor TimeOut (.clock(clock_1_out), .Q4(TimeOut_q4), .Q3(TimeOut_q3), .Q2(TimeOut_q2), .Q1(TimeOut_q1));
  Button _1 (.out(_1_out));
  Button _4 (.out(_4_out));
  Button _7 (.out(_7_out));
  Clock clock_1 (.out(clock_1_out));
  nor nor_1 (nor_1_out, TimeOut_q4, TimeOut_q3, TimeOut_q2, TimeOut_q1);
  Button _2 (.out(_2_out));
  Button _5 (.out(_5_out));
  Button _8 (.out(_8_out));
  Button _0 (.out(_0_out));
  Button button_1 (.out(button_1_out));
  J_K_Flip_Flop j_k_ff_1 (.J(1'b1), .clk(nor_1_out), .K(1'b1), .Q(j_k_ff_1_q));  // open: Qn, preset, en, reset
  Button _3 (.out(_3_out));
  Button _6 (.out(_6_out));
  Button _9 (.out(_9_out));
  Button Enter (.out(Enter_out));
  Button button_2 (.out(button_2_out));
  Button Reset (.out(Reset_out));
  MOD_3_Counter mod_3_counter_1 (
    .Clock(n4_bit_encoder_1_active), .Q2(mod_3_counter_1_q2[0]), .Q1(mod_3_counter_1_q2[1]), .Reset(or_1_out));
  or or_1 (or_1_out, Reset_out, j_k_ff_1_q);
  Decoder #(.select(2)) decoder_1 (
    .out0(decoder_1_out0), .out1(decoder_1_out1), .out2(decoder_1_out2), .out3(decoder_1_out3),
    .sel(mod_3_counter_1_q2));  // open: en
  _4_bit_Encoder u_4_bit_encoder_1 (
    ._0(_0_out), ._1(_1_out), .A4(n4_bit_encoder_1_a1[3]), ._2(_2_out), ._3(_3_out), ._4(_4_out),
    .A3(n4_bit_encoder_1_a1[2]), ._5(_5_out), ._6(_6_out), ._7(_7_out), .A2(n4_bit_encoder_1_a1[1]),
    ._8(_8_out), ._9(_9_out), .A1(n4_bit_encoder_1_a1[0]), .Active(n4_bit_encoder_1_active));
  Register #(.width(4)) register_1 (
    .D(n4_bit_encoder_1_a1), .Q(register_1_q), .clk(decoder_1_out1), .clr(or_1_out));  // open: en
  Register #(.width(4)) register_2 (
    .D(n4_bit_encoder_1_a1), .Q(register_2_q), .clk(decoder_1_out2), .clr(or_1_out));  // open: en
  Register #(.width(4)) register_3 (
    .D(n4_bit_encoder_1_a1), .Q(register_3_q), .clk(decoder_1_out3), .clr(or_1_out));  // open: en
  Register #(.width(4)) register_4 (
    .D(n4_bit_encoder_1_a1), .Q(register_4_q), .clk(decoder_1_out0), .clr(or_1_out));  // open: en
  Register #(.width(4)) register_5 (
    .D(register_1_q), .Q(register_5_q), .clk(button_1_out), .clr(button_2_out));  // open: en
  Register #(.width(4)) register_6 (
    .D(register_2_q), .Q(register_6_q), .clk(button_1_out), .clr(button_2_out));  // open: en
  Register #(.width(4)) register_7 (
    .D(register_3_q), .Q(register_7_q), .clk(button_1_out), .clr(button_2_out));  // open: en
  Register #(.width(4)) register_8 (
    .D(register_4_q), .Q(register_8_q), .clk(button_1_out), .clr(button_2_out));  // open: en
  Comparator #(.width(4)) comparator_1 (.a(register_1_q), .b(register_5_q), .eq(comparator_1_eq));  // open: gt, lt
  Comparator #(.width(4)) comparator_2 (.a(register_2_q), .b(register_6_q), .eq(comparator_2_eq));  // open: gt, lt
  Comparator #(.width(4)) comparator_3 (.a(register_3_q), .b(register_7_q), .eq(comparator_3_eq));  // open: gt, lt
  Comparator #(.width(4)) comparator_4 (.a(register_4_q), .b(register_8_q), .eq(comparator_4_eq));  // open: gt, lt
  and and_1 (and_1_out, comparator_1_eq, comparator_2_eq, Enter_out, comparator_3_eq, comparator_4_eq);

  // Notes on the sheet:
  //   4-bit_Decoder
  //   Setting PasWord
  //   StoredPIN_Reset
  //   MOD-3_Counter
  //   4-bit Encoder
  //   Stored_PIN
  //   Input_PIN
endmodule

module _4_bit_Encoder (
  input  _0,
  input  _1,
  input  _2,
  input  _3,
  input  _4,
  input  _5,
  input  _6,
  input  _7,
  input  _8,
  input  _9,
  output A4,
  output A3,
  output A2,
  output A1,
  output Active
);

  wire or_5_out, or_6_out;

  or or_1 (A4, _8, _9);
  or or_2 (A3, _4, _7, _6, _5);
  or or_3 (A2, _2, _3, _6, _7);
  or or_4 (A1, _1, _3, _5, _7, _9);
  or or_5 (or_5_out, _0, _1, _2, _3, _7);
  or or_6 (or_6_out, _4, _5, _6, _8, _9);
  or or_7 (Active, or_5_out, or_6_out);
endmodule

module Check_PassWord (
  input  [3:0] Input_PIN,
  output Output
);

  wire and_1_out, and_3_out, Enter_out, j_k_ff_1_q, j_k_ff_2_q, not_1_out, not_2_out, or_1_out;
  wire [3:0] xor_1_out;

  Button Enter (.out(Enter_out));
  assign xor_1_out = Input_PIN ^ 4'b0011;  // XOR_Gate xor_1, 4 bits wide
  or or_1 (or_1_out, xor_1_out[0], xor_1_out[1], xor_1_out[2], xor_1_out[3]);
  not not_1 (not_1_out, and_3_out);
  not not_2 (not_2_out, or_1_out);
  and and_1 (and_1_out, or_1_out, not_1_out, Enter_out);
  and and_2 (Output, not_1_out, Enter_out, not_2_out);
  J_K_Flip_Flop #(.trigger("falling")) j_k_ff_1 (
    .J(1'b1), .clk(and_1_out), .K(1'b1), .Q(j_k_ff_1_q));  // open: Qn, preset, en, reset
  and and_3 (and_3_out, j_k_ff_1_q, j_k_ff_2_q);
  J_K_Flip_Flop #(.trigger("falling")) j_k_ff_2 (
    .J(1'b1), .clk(j_k_ff_1_q), .K(1'b1), .Q(j_k_ff_2_q));  // open: Qn, preset, en, reset

  // Notes on the sheet:
  //   stored_PIN
endmodule

module MOD_3_Counter (
  input  Clock,
  input  Reset,
  output Q2,
  output Q1
);

  wire and_1_out;

  J_K_Flip_Flop j_k_ff_1 (.J(1'b1), .clk(Clock), .K(1'b1), .Q(Q2), .reset(Reset));  // open: Qn, preset, en
  J_K_Flip_Flop j_k_ff_2 (.J(Q2), .clk(Clock), .K(Q2), .Q(Q1), .reset(Reset));  // open: Qn, preset, en
  and and_1 (and_1_out, Q2, Q1);
endmodule

module TimeOutSensor (
  input  clock,
  output Q4,
  output Q3,
  output Q2,
  output Q1
);

  wire and_1_out, and_2_out, and_3_out;

  J_K_Flip_Flop j_k_ff_1 (.J(1'b1), .clk(clock), .K(1'b1), .Q(Q4), .reset(and_3_out));  // open: Qn, preset, en
  J_K_Flip_Flop j_k_ff_2 (.J(Q4), .clk(clock), .K(Q4), .Q(Q3), .reset(and_3_out));  // open: Qn, preset, en
  and and_1 (and_1_out, Q4, Q3);
  and and_2 (and_2_out, and_1_out, Q2);
  J_K_Flip_Flop j_k_ff_3 (
    .J(and_1_out), .clk(clock), .K(and_1_out), .Q(Q2), .reset(and_3_out));  // open: Qn, preset, en
  J_K_Flip_Flop j_k_ff_4 (
    .J(and_2_out), .clk(clock), .K(and_2_out), .Q(Q1), .reset(and_3_out));  // open: Qn, preset, en
  and and_3 (and_3_out, Q1, Q3);
endmodule

module _7_segment_decoder (
  input  D,
  input  C,
  input  B,
  input  A,
  output a_2,
  output b_2,
  output c_2,
  output d_2,
  output e,
  output f,
  output g
);

  wire and_1_out, and_2_out, and_3_out, and_4_out, and_5_out, and_6_out, and_7_out, and_8_out, and_9_out,
       and_10_out, and_11_out, and_12_out, and_13_out, and_14_out, and_15_out, and_16_out, not_1_out,
       not_2_out, not_3_out, not_4_out, not_5_out, not_6_out, not_7_out, not_8_out, not_9_out, not_10_out,
       not_11_out, not_12_out, not_13_out, not_14_out, not_15_out, not_16_out, not_17_out, not_18_out,
       not_19_out, not_20_out, not_21_out;

  not not_1 (not_1_out, C);
  and and_1 (and_1_out, not_1_out, not_2_out);
  not not_2 (not_2_out, A);
  and and_2 (and_2_out, C, A);
  not not_3 (not_3_out, C);
  not not_4 (not_4_out, B);
  and and_3 (and_3_out, not_4_out, not_5_out);
  not not_5 (not_5_out, A);
  and and_4 (and_4_out, B, A);
  not not_6 (not_6_out, B);
  or or_1 (c_2, not_6_out, A, C);
  not not_7 (not_7_out, C);
  and and_5 (and_5_out, not_7_out, not_8_out);
  not not_8 (not_8_out, A);
  not not_9 (not_9_out, C);
  and and_6 (and_6_out, not_9_out, B);
  and and_7 (and_7_out, B, not_10_out);
  not not_10 (not_10_out, A);
  and and_8 (and_8_out, C, not_11_out, A);
  not not_11 (not_11_out, B);
  not not_12 (not_12_out, C);
  and and_9 (and_9_out, not_12_out, not_13_out);
  not not_13 (not_13_out, A);
  and and_10 (and_10_out, B, not_14_out);
  not not_14 (not_14_out, A);
  not not_15 (not_15_out, B);
  and and_11 (and_11_out, not_15_out, not_16_out);
  not not_16 (not_16_out, A);
  and and_12 (and_12_out, C, not_17_out);
  not not_17 (not_17_out, B);
  and and_13 (and_13_out, C, not_18_out);
  not not_18 (not_18_out, A);
  not not_19 (not_19_out, C);
  and and_14 (and_14_out, not_19_out, B);
  and and_15 (and_15_out, C, not_20_out);
  not not_20 (not_20_out, B);
  and and_16 (and_16_out, C, not_21_out);
  not not_21 (not_21_out, A);
  or or_2 (a_2, and_1_out, B, and_2_out, D);
  or or_3 (b_2, not_3_out, and_3_out, and_4_out);
  or or_4 (d_2, and_5_out, and_6_out, and_7_out, and_8_out, D);
  or or_5 (e, and_9_out, and_10_out);
  or or_6 (f, and_11_out, and_12_out, and_13_out, D);
  or or_7 (g, and_14_out, and_15_out, and_16_out, D);
endmodule
